# Fritzing sketch Untitled Sketch 3 (saved by Fritzing 0.9.3b)
breadboards: 1

parts:
  KY-2 = Keyes Relay [package=THT]
  M2 = DC Motor
  hc-sr2 = hc-sr04
  VCC2 = Battery block 9V
  U1 = ESP8266 NodeMCU LoLin module

nets:
  N1: KY-2.signal, U1.D8
  VCC: KY-2.power, hc-sr2.VCC, VCC2.+, U1.Vin
  GND: KY-2.ground, hc-sr2.GND, VCC2.-, U1.GND
  N2: KY-2.NC, M2.pin_1
  N3: hc-sr2.Trig, U1.D6
  N4: hc-sr2.Echo, U1.D5

notes:
  connect with AC mains for big water pump/ for test, connect with battery and use small motor
  pin1- input
  pin2-Vcc
  pin3- GND
  1. NC- normally closed
  2. common
  3. NO- normally open

custom parts:
  Keyes Relay: The Keyes 5V relay module is suitable for SCM development, home appliance control. It uses a 5V~12V TIL control signal which can control DC / AC signal.
  ESP8266 NodeMCU LoLin module: ESP8266 based NodeMCU
