# Fritzing sketch Untitled Sketch (saved by Fritzing 0.9.3b)
breadboards: 1

parts:
  KY-1 = Keyes Relay [package=THT]
  Part1 = Arduino Uno (Rev3)
  M1 = DC Motor
  hc-sr1 = hc-sr04
  VCC1 = Battery block 9V

nets:
  N1: KY-1.signal, Part1.D9_PWM
  5V: KY-1.power, Part1.5V, hc-sr1.VCC
  GND: KY-1.ground, Part1.GND, hc-sr1.GND, VCC1.-
  N2: KY-1.NC, M1.pin_1
  N3: Part1.D5_PWM, hc-sr1.Echo
  N4: Part1.D6_PWM, hc-sr1.Trig
  N5: Part1.VIN, VCC1.+

notes:
  connect with AC mains for big water pump/ for test, connect with battery and use small motor
  pin1- input
  pin2-Vcc
  pin3- GND
  1. NC- normally closed
  2. common
  3. NO- normally open

custom parts:
  Keyes Relay: The Keyes 5V relay module is suitable for SCM development, home appliance control. It uses a 5V~12V TIL control signal which can control DC / AC signal.
